# Fritzing sketch segments (saved by Fritzing 0.9.0b)
circuit board: 8.46667cm x 5.64444cm
breadboards: 1

parts:
  Composant1 = Arduino Due (Rev2b)
  R1 = Trimmer Potentiometer [maximum_resistance=10kΩ package=THT]
  R2 = Resistor [tolerance=±5% resistance=220 package=THT]
  R3 = Resistor [tolerance=±5% resistance=220 package=THT]
  U1 = 7-SEGMENT-DISPLAY-1_-RED [package=7-segment-1_pth]
  U2 = 7-SEGMENT-DISPLAY-1_-RED [package=7-segment-1_pth]

nets:
  N1: Composant1.A0, R1.wiper
  N2: Composant1.D14/TX3, U2.A
  N3: Composant1.D15/RX3, U2.B
  N4: Composant1.D16/TX2, U2.C
  N5: Composant1.D17/RX2, U2.DP
  N6: Composant1.D18/TX1, U2.F
  N7: Composant1.D19/RX1, U2.G
  N8: Composant1.D8_PWM, U1.G
  N9: Composant1.D9_PWM, U1.F
  N10: Composant1.D10_PWM/SS0, U1.E
  N11: Composant1.D11_PWM, U1.D
  N12: Composant1.GND, R1.leg1, R2.Pin_0, R3.Pin_0
  N13: Composant1.D2_PWM, U2.E
  N14: Composant1.D3_PWM, U2.D
  N15: Composant1.D4_PWM/SS1, U1.DP
  N16: Composant1.D5_PWM, U1.C
  N17: Composant1.D6_PWM, U1.B
  N18: Composant1.D7_PWM, U1.A
  N19: Composant1.5V, R1.leg2
  N20: R2.Pin_1, U1.G1
  N21: R3.Pin_1, U2.G1
